// Logisim project A.circ as structural Verilog
module circuitoa (
  input  a,
  input  b,
  input  c,
  input  d,
  output out_5
);

  wire and_1_out, and_2_out, and_3_out;

  and and_1 (and_1_out, ~a, ~b, c);  // AND_Gate
  and and_2 (and_2_out, ~a, b, ~c);  // AND_Gate
  and and_3 (and_3_out, a, ~b, ~c);  // AND_Gate
  or or_1 (out_5, and_1_out, and_2_out, and_3_out);
endmodule
