// Logisim project 2boletin1.2 nor corregido.circ as structural Verilog: 1 circuit, main circuit main
module main (
  input  A,
  input  B,
  input  C,
  input  D,
  output out_5
);

  wire nor_1_out, nor_2_out, nor_3_out;

  nor nor_1 (nor_1_out, ~A, ~B);  // NOR_Gate
  nor nor_2 (nor_2_out, ~A, ~C);  // NOR_Gate
  nor nor_3 (nor_3_out, nor_1_out, nor_2_out);
  not nor_4 (out_5, nor_3_out);  // NOR_Gate
endmodule
