// Logisim project D.circ as structural Verilog: 1 circuit, main circuit main
module main (
  input  A,
  input  B,
  input  C,
  input  in_4
);

  wire and_1_out, and_2_out, and_3_out, or_1_out;

  and and_1 (and_1_out, B, C);
  and and_2 (and_2_out, B, in_4);
  and and_3 (and_3_out, C, in_4);
  or or_1 (or_1_out, and_1_out, and_2_out, and_3_out);
  LED led_1 (.in(or_1_out));
endmodule
