// Logisim project EJERCICIO 2.1.circ as structural Verilog: 1 circuit, main circuit main
module main (
  input  A,
  input  B,
  input  C,
  input  D,
  output out_5
);

  wire and_1_out, and_2_out;

  and and_1 (and_1_out, A, B);
  and and_2 (and_2_out, A, C);
  or or_1 (out_5, and_1_out, and_2_out);
endmodule
