// Logisim project a,b,c,d.circ as structural Verilog: 3 circuits, main circuit c
module c (
  input  A,
  input  B,
  input  C,
  input  D,
  output out_5
);

  wire and_1_out, and_2_out, and_3_out;

  and and_1 (and_1_out, A, B);
  and and_2 (and_2_out, ~B, C, ~D);  // AND_Gate
  and and_3 (and_3_out, ~C, ~B, D);  // AND_Gate
  or or_1 (out_5, and_1_out, and_2_out, and_3_out);
endmodule

module D (
  input  A,
  input  B,
  input  C,
  input  in_4,
  output out_5
);

  wire and_1_out, and_2_out, and_3_out;

  and and_1 (and_1_out, B, C);
  and and_2 (and_2_out, B, in_4);
  and and_3 (and_3_out, C, in_4);
  or or_1 (out_5, and_1_out, and_2_out, and_3_out);
endmodule

module a (
  input  a,
  input  b,
  input  c,
  input  d,
  output out_5
);

  wire and_1_out, and_2_out, and_3_out;

  and and_1 (and_1_out, ~a, ~b, c);  // AND_Gate
  and and_2 (and_2_out, ~a, b, ~c);  // AND_Gate
  and and_3 (and_3_out, a, ~b, ~c);  // AND_Gate
  or or_1 (out_5, and_1_out, and_2_out, and_3_out);
endmodule
