// Logisim project b.circ as structural Verilog
module circuitoa (
  input  a,
  input  b,
  input  c,
  input  d,
  output out_5
);

  wire and_1_out, and_2_out, and_3_out;

  and and_1 (and_1_out, ~a, b, ~c, ~d);  // AND_Gate
  and and_2 (and_2_out, ~b, d);  // AND_Gate
  and and_3 (and_3_out, a, c);
  // OR_Gate or_1 has open pins: in1=and_1_out, in2=and_2_out, in3=and_3_out, out=open
endmodule
