// Logisim project circuitoa.circ as structural Verilog
module circuitoa (
  input  a,
  input  b,
  input  c,
  input  d
);

  wire and_1_out, and_2_out, and_3_out, controlled_inverter_1_out, controlled_inverter_2_out,
       controlled_inverter_4_out, or_1_out;

  Controlled_Inverter controlled_inverter_1 (.in(a), .out(controlled_inverter_1_out));  // open: en
  assign controlled_inverter_2_out = b ? ~b : 1'bz;  // Controlled_Inverter controlled_inverter_2
  assign c = c ? ~c : 1'bz;  // Controlled_Inverter controlled_inverter_3
  Controlled_Inverter controlled_inverter_4 (.in(d), .out(controlled_inverter_4_out));  // open: en
  and and_1 (and_1_out, a, c);
  and and_2 (and_2_out, d, controlled_inverter_2_out);
  and and_3 (and_3_out, controlled_inverter_1_out, c, controlled_inverter_4_out, b);
  LED led_1 (.in(or_1_out));
  or or_1 (or_1_out, and_1_out, and_2_out, and_3_out);
endmodule
