// Logisim project 2boletin2.circ as structural Verilog: 1 circuit, main circuit main
module main (
  input  [3:0] A,
  input  [3:0] in_2,
  input  [3:0] B,
  input  [3:0] C,
  output [3:0] out_5,
  output out_6
);

  wire comparator_1_lt;
  wire [3:0] multiplexer_1_out;

  Comparator #(.width(4)) comparator_1 (.a(B), .b(C), .lt(comparator_1_lt));  // open: gt, eq
  Multiplexer #(.width(4)) multiplexer_1 (
    .in0(B), .in1(C), .out(multiplexer_1_out), .sel(comparator_1_lt));  // open: en
  _1boletin2_main main_1 (.in_1(A), .in_2(multiplexer_1_out), .in_3(in_2), .out_4(out_5), .out_5(out_6));
endmodule
