// Logisim project 3.2.circ as structural Verilog: 1 circuit, main circuit main
module main (
  input  [3:0] in_1,
  input  [3:0] in_2,
  input  [3:0] in_3,
  input  [3:0] in_4,
  input  suma_resta,
  input  C1_C2,
  output [3:0] out_7
);

  wire adder_1_cout;
  wire [3:0] adder_1_out, adder_2_out, adder_3_out, adder_4_out, multiplexer_1_out, not_1_out;

  assign not_1_out = ~in_4;  // NOT_Gate not_1, 4 bits wide
  Adder #(.width(4)) adder_1 (.a(in_2), .b(in_4), .out(adder_1_out), .cout(adder_1_cout));  // open: cin
  Adder #(.width(4)) adder_2 (.a(in_3), .b(not_1_out), .out(adder_2_out));  // open: cin, cout
  Multiplexer #(.width(4)) multiplexer_1 (
    .in0(adder_1_out), .in1(adder_3_out), .out(multiplexer_1_out), .sel(suma_resta));  // open: en
  Adder #(.width(4)) adder_3 (.a(in_2), .b(adder_2_out), .out(adder_3_out));  // open: cin, cout
  Adder #(.width(4)) adder_4 (.a(in_1), .b(multiplexer_1_out), .out(adder_4_out), .cin(adder_1_cout));  // open: cout
  Multiplexer #(.width(4)) multiplexer_2 (
    .in0(adder_4_out), .in1(multiplexer_1_out), .out(out_7), .sel(C1_C2));  // open: en
endmodule
