// Logisim project P1.circ as structural Verilog: 1 circuit, main circuit main
module main (
  input  [1:0] in_1,
  output y1__Lata,
  output y0__Cambio
);

  wire and_1_out, and_2_out, and_3_out, and_4_out, and_5_out, and_6_out, and_7_out, and_8_out, D0__q0_q,
       D0__q0_qn, D1__q1_q, D1__q1_qn, not_1_out, not_2_out, or_1_out, or_2_out, or_3_out, or_4_out, R1_out;

  Clock R1 (.out(R1_out));
  not not_1 (not_1_out, in_1[0]);
  not not_2 (not_2_out, in_1[1]);
  and and_1 (and_1_out, D0__q0_q, not_1_out, not_2_out);
  and and_2 (and_2_out, D0__q0_qn, in_1[0], D1__q1_qn);
  or or_1 (or_1_out, and_1_out, and_2_out);
  and and_3 (and_3_out, D1__q1_qn, D0__q0_qn, in_1[1]);
  or or_2 (or_2_out, and_3_out, and_4_out, and_5_out);
  and and_4 (and_4_out, D0__q0_q, in_1[0]);
  and and_5 (and_5_out, not_2_out, not_1_out, D1__q1_q);
  or or_3 (or_3_out, in_1[0], in_1[1]);
  D_Flip_Flop D0__q0 (.clk(R1_out), .D(or_1_out), .Q(D0__q0_q), .Qn(D0__q0_qn));  // open: preset, en, reset
  D_Flip_Flop D1__q1 (.clk(R1_out), .D(or_2_out), .Q(D1__q1_q), .Qn(D1__q1_qn));  // open: preset, en, reset
  and and_6 (and_6_out, D1__q1_q, or_3_out);
  and and_7 (and_7_out, in_1[1], D1__q1_q);
  and and_8 (and_8_out, D0__q0_q, in_1[1]);
  or or_4 (or_4_out, and_8_out, and_6_out);
  D_Flip_Flop D3__y1 (.clk(R1_out), .D(or_4_out), .Q(y1__Lata));  // open: Qn, preset, en, reset
  D_Flip_Flop D2__y0 (.clk(R1_out), .D(and_7_out), .Q(y0__Cambio));  // open: Qn, preset, en, reset

  // Notes on the sheet:
  //   ¬e0
  //   CLk
  //   e0
  //   ¬e1
  //   e1
  //   ¬q1
  //   q1
  //   q0
  //   ¬q0
endmodule
