// Logisim project registro.circ as structural Verilog: 3 circuits, main circuit main
module main (
  input  CLK,
  input  \input ,
  input  clear,
  input  D1,
  input  D2,
  input  D3,
  input  D4,
  input  [1:0] Accionador,
  output out_9,
  output out_10,
  output out_11,
  output out_12
);

  wire multiplexer_1_out, multiplexer_2_out, multiplexer_3_out, multiplexer_4_out;

  Multiplexer #(.select(2)) multiplexer_1 (
    .in0(\input ), .in1(out_10), .in2(D1), .in3(out_9), .out(multiplexer_1_out), .sel(Accionador));  // open: en
  D_Flip_Flop d_ff_1 (.clk(CLK), .D(multiplexer_1_out), .Q(out_9), .reset(clear));  // open: Qn, preset, en
  D_Flip_Flop d_ff_2 (.clk(CLK), .D(multiplexer_2_out), .Q(out_10), .reset(clear));  // open: Qn, preset, en
  Multiplexer #(.select(2)) multiplexer_2 (
    .in0(out_9), .in1(out_11), .in2(D2), .in3(out_10), .out(multiplexer_2_out), .sel(Accionador));  // open: en
  Multiplexer #(.select(2)) multiplexer_3 (
    .in0(out_10), .in1(out_12), .in2(D3), .in3(out_11), .out(multiplexer_3_out), .sel(Accionador));  // open: en
  D_Flip_Flop d_ff_3 (.clk(CLK), .D(multiplexer_3_out), .Q(out_11), .reset(clear));  // open: Qn, preset, en
  Multiplexer #(.select(2)) multiplexer_4 (
    .in0(out_11), .in1(out_9), .in2(D4), .in3(out_12), .out(multiplexer_4_out), .sel(Accionador));  // open: en
  D_Flip_Flop d_ff_4 (.clk(CLK), .D(multiplexer_4_out), .Q(out_12), .reset(clear));  // open: Qn, preset, en

  // Notes on the sheet:
  //   00 derecha
  //   01 Izquierda
  //   10 carga
  //   11 mantenimiento
  //   PROBLEMA CONTADOR: DESPLAZAMIENTO A LA DERECHA
endmodule

module Ej_3 (
  input  in_1,
  input  in_2,
  input  in_3,
  input  in_4,
  input  [1:0] in_5,
  input  in_6,
  output out_7,
  output out_8,
  output out_9,
  output out_10
);

  wire a1, a2, a3, d_ff_1_qn, d_ff_2_qn, d_ff_3_qn;
  wire [0:0] a3_out;

  D_Flip_Flop d_ff_1 (.clk(in_6), .D(d_ff_1_qn), .Q(a1), .Qn(d_ff_1_qn));  // open: preset, en, reset
  D_Flip_Flop d_ff_2 (.clk(d_ff_1_qn), .D(d_ff_2_qn), .Q(a2), .Qn(d_ff_2_qn));  // open: preset, en, reset
  D_Flip_Flop d_ff_3 (.clk(d_ff_2_qn), .D(d_ff_3_qn), .Q(a3), .Qn(d_ff_3_qn));  // open: preset, en, reset
  main main_1 (
    .D2(in_2), .D3(in_3), .D4(in_4), .Accionador(in_5), .D1(in_1), .CLK(in_6), .out_9(out_7), .out_10(out_8),
    .out_11(out_9), .out_12(out_10));  // open: input, clear
  // AND_Gate and_1 has open pins: in0=a1, in1=a2, in2=a3, out=open
  or u_a3 (a3_out[0], a1, a3);

  // Notes on the sheet:
  //   00 derecha
  //   01 Izquierda
  //   10 carga
  //   11 mantenimiento
endmodule

module nue (
  input  in_1,
  input  in_2,
  input  in_3,
  input  in_4,
  input  in_5,
  output D0,
  output D1,
  output D2,
  output D3
);

  wire and_1_out, and_2_out, and_3_out, and_4_out, multiplexer_1_out, multiplexer_2_out, multiplexer_3_out,
       multiplexer_4_out, or_1_out, Qa, Qb, Qc, R;
  wire [1:0] S;

  Multiplexer #(.select(2), .enable("false")) multiplexer_1 (
    .in0(1'b0), .in1(D3), .in2(D1), .in3(in_2), .out(multiplexer_1_out), .sel(S));
  D_Flip_Flop d_ff_1 (.clk(R), .D(multiplexer_1_out), .Q(D0), .reset(in_1));  // open: Qn, preset, en
  Multiplexer #(.select(2), .enable("false")) multiplexer_2 (
    .in0(1'b0), .in1(D0), .in2(D2), .in3(in_3), .out(multiplexer_2_out), .sel(S));
  Clock clock_1 (.out(R));
  D_Flip_Flop d_ff_2 (.clk(R), .D(multiplexer_2_out), .Q(D1), .reset(in_1));  // open: Qn, preset, en
  and and_1 (and_1_out, ~Qa, Qb, Qc);  // AND_Gate
  Multiplexer #(.select(2), .enable("false")) multiplexer_3 (
    .in0(1'b0), .in1(D1), .in2(D3), .in3(in_4), .out(multiplexer_3_out), .sel(S));
  D_Flip_Flop Da (.clk(R), .D(and_1_out), .Q(Qa));  // open: Qn, preset, en, reset
  D_Flip_Flop d_ff_3 (.clk(R), .D(multiplexer_3_out), .Q(D2), .reset(in_1));  // open: Qn, preset, en
  and and_2 (and_2_out, Qc, ~Qb, ~Qa);  // AND_Gate
  and and_3 (and_3_out, ~Qc, Qb, ~Qa);  // AND_Gate
  Multiplexer #(.select(2), .enable("false")) multiplexer_4 (
    .in0(1'b0), .in1(D2), .in2(D0), .in3(in_5), .out(multiplexer_4_out), .sel(S));
  D_Flip_Flop Db (.clk(R), .D(or_1_out), .Q(Qb));  // open: Qn, preset, en, reset
  or or_1 (or_1_out, and_2_out, and_3_out);
  Multiplexer #(.select(3), .width(2), .enable("false")) multiplexer_5 (
    .in0(2'b01), .in1(2'b11), .in2(2'b10), .in3(2'b00), .in4(2'b11), .out(S), .sel({Qa, Qb, Qc}));  // open: in5, in6, in7
  D_Flip_Flop d_ff_4 (.clk(R), .D(multiplexer_4_out), .Q(D3), .reset(in_1));  // open: Qn, preset, en
  D_Flip_Flop Dc (.clk(R), .D(and_4_out), .Q(Qc));  // open: Qn, preset, en, reset
  and and_4 (and_4_out, ~Qa, ~Qc);  // AND_Gate

  // Other names for the same wires on the sheet: B = D1; C = D2; clear = in_1; D = D3; d0_t = in_2; d1_t = in_3;
  //   d2_t = in_4; d3_t = in_5; A = D0; I = D0

  // Notes on the sheet:
  //   01--->desplazamiento a a derecha
  //   11--->carga en paralelo
  //   00--->borrado de los cuatro bits
  //   11--->carga en paralelo
  //   10--->desplazamiento a la izquierda
endmodule
