// Logisim project archivo.circ as structural Verilog: 1 circuit, main circuit main
module main (
  input  in_1,
  input  in_2,
  output out_3,
  output [2:0] out_4,
  output [2:0] out_5,
  output out_6
);

  wire and_1_out, and_2_out, clock_1_out, not_2_out, not_3_out, not_4_out;

  not not_1 (out_6, out_3);
  Clock clock_1 (.out(clock_1_out));
  Counter #(.width(3), .max('h7)) counter_1 (
    .load(out_3), .D({out_4[2:1], in_1}), .count(out_6), .Q({out_4[1], out_4[2], out_5[0]}),
    .clk(clock_1_out), .clr(in_2));  // open: carry
  not not_2 (not_2_out, out_4[1]);
  not not_3 (not_3_out, out_4[2]);
  not not_4 (not_4_out, out_5[0]);
  and and_1 (and_1_out, out_4[1], not_3_out, out_5[0]);
  and and_2 (and_2_out, not_2_out, out_4[2], not_4_out);
  or or_1 (out_3, and_2_out, and_1_out);

  assign out_4[0] = in_1;
  assign out_5[2:1] = {out_4[1], out_4[2]};

  // Notes on the sheet:
  //   Load=1;Count=0 : Fuerza Carga síncrona
  //   Load: Decide si hay carga síncrona(1)
  //   Load =0;Count=1: Incrementa en 1 el valor actual
endmodule
