// Logisim project cosa.circ as structural Verilog: 1 circuit, main circuit main
module main (
  input  in_1,
  input  in_2,
  output out_3
);

  wire and_1_out, and_2_out, and_3_out, and_4_out, and_5_out, clock_1_out, not_1_out, not_2_out, or_1_out,
       or_2_out, Q0_qn, Q1_q, Q1_qn;

  Clock clock_1 (.out(clock_1_out));
  not not_1 (not_1_out, in_1);
  not not_2 (not_2_out, in_2);
  and and_1 (and_1_out, not_1_out, in_2, Q1_qn);
  and and_2 (and_2_out, in_1, Q1_q);
  and and_3 (and_3_out, in_1, not_2_out);
  and and_4 (and_4_out, in_1, Q1_q);
  and and_5 (and_5_out, in_1, out_3);
  or or_1 (or_1_out, and_4_out, and_5_out);
  or or_2 (or_2_out, and_1_out, and_2_out, and_3_out);
  D_Flip_Flop Q1 (.clk(clock_1_out), .D(or_2_out), .Q(Q1_q), .Qn(Q1_qn));  // open: preset, en, reset
  D_Flip_Flop Q0 (.clk(clock_1_out), .D(or_1_out), .Q(out_3), .Qn(Q0_qn));  // open: preset, en, reset

  // Notes on the sheet:
  //   q0
  //   ¬q0
  //   ¬q1
  //   q1
  //   e0
  //   e1
  //   ¬e0
  //   ¬e1
endmodule
