// Logisim project 3.2.circ as structural Verilog: 1 circuit, main circuit main
module main (
  input  [3:0] in_1,
  input  [3:0] in_2,
  input  [3:0] in_3,
  input  in_4,
  input  C1_C2,
  output out_6,
  output [3:0] out_7
);

  wire adder_1_cout, and_1_out, and_2_out, and_3_out, and_4_out, and_5_out, and_6_out, or_2_out;
  wire [3:0] adder_1_out, xor_1_out;

  and and_1 (and_1_out, in_1[3], xor_1_out[3]);
  and and_2 (and_2_out, ~in_1[3], ~xor_1_out[3]);  // AND_Gate
  Adder #(.width(4)) adder_1 (.a(in_1), .b(xor_1_out), .out(adder_1_out), .cin(and_3_out), .cout(adder_1_cout));
  assign xor_1_out = {4{in_4}} ^ in_3;  // XOR_Gate xor_1, 4 bits wide
  and and_3 (and_3_out, C1_C2, in_4);
  and and_4 (and_4_out, adder_1_cout, ~C1_C2);  // AND_Gate
  or or_1 (out_6, or_2_out, adder_1_cout);
  Adder #(.width(4)) adder_2 (.a(adder_1_out), .b(in_2), .out(out_7), .cin(and_4_out));  // open: cout
  and and_5 (and_5_out, and_1_out, ~out_7[3]);  // AND_Gate
  and and_6 (and_6_out, and_2_out, out_7[3]);
  or or_2 (or_2_out, and_5_out, and_6_out);
endmodule
