// Logisim project Ej3.circ as structural Verilog: 1 circuit, main circuit main
module main (
  input  [3:0] in_1,
  input  [3:0] in_2,
  input  in_3,
  input  in_4,
  output [3:0] out_5,
  output out_6,
  output out_7
);

  wire [3:0] C1, C2, multiplexer_1_out, multiplexer_2_out, not_1_out, not_2_out;

  assign not_1_out = ~in_1;  // NOT_Gate not_1, 4 bits wide
  assign not_2_out = ~in_2;  // NOT_Gate not_2, 4 bits wide
  Multiplexer #(.width(4)) multiplexer_1 (
    .in0(in_1), .in1(not_1_out), .out(multiplexer_1_out), .sel(in_3));  // open: en
  Multiplexer #(.width(4)) multiplexer_2 (
    .in0(in_2), .in1(not_2_out), .out(multiplexer_2_out), .sel(in_3));  // open: en
  Adder #(.width(4)) adder_1 (.a(multiplexer_1_out), .b(multiplexer_2_out), .out(C2), .cout(out_6));  // open: cin
  Adder #(.width(4)) adder_2 (.a(multiplexer_1_out), .b(multiplexer_2_out), .out(C1), .cin(out_7), .cout(out_7));
  Multiplexer #(.width(4)) multiplexer_3 (.in0(C2), .in1(C1), .out(out_5), .sel(in_4));  // open: en

  // Other names for the same wires on the sheet: Res[3:0] = in_1; Res2[3:0] = in_2; SUM2[3:0] = in_2;
  //   SUMA_RESTA = in_3
endmodule
