// Logisim project q.circ as structural Verilog: 1 circuit, main circuit main
// 0
module main (
  input  in_1,
  input  [3:0] in_2,
  input  [3:0] in_3,
  input  [3:0] in_4,
  output out_5,
  output out_6,
  output out_7,
  output out_8,
  output [3:0] out_9,
  output out_10
);

  wire [3:0] adder_2_out, main_1_p4;

  Adder #(.width(4)) adder_1 (.a(in_2), .b(in_3), .out({out_8, out_7, out_6, out_5}), .cin(in_1));  // open: cout
  // EJERCICIO_2_1_main main_1: pin names not known; wires that end beside it: out_8, out_7, out_6, main_1_p4, out_5
  Multiplexer #(.width(4)) multiplexer_1 (.out(main_1_p4), .sel(out_9[0]), .en(out_5));  // open: in0, in1
  Adder #(.width(4)) adder_2 (
    .a(in_4), .b({out_8, out_7, out_6, out_5}), .out(adder_2_out), .cout(out_10));  // open: cin
  Multiplexer #(.width(4)) multiplexer_2 (
    .in0(adder_2_out), .in1({out_8, out_7, out_6, out_5}), .out(out_9), .sel(out_10));  // open: en
  // Pins of 1 and 4 bits meet at {out_8, out_7, out_6, out_5}
  // Pins of 1 and 4 bits meet at out_9
endmodule
